# Fritzing sketch FritzingSchematic (saved by Fritzing 0.8.7b)

parts:
  Part2 = Arduino Uno (Rev3)
  TFT2 = 1.8" TFT Display with uSD
  DHT1 = DHT22 Humidity and Temperature Sensor

nets:
  N1: Part2.A0, DHT1.DATA
  N2: Part2.D8, TFT2.RST
  N3: Part2.D9_PWM, TFT2.D/C
  N4: Part2.D10_PWM/SS, TFT2.CS
  N5: Part2.D11_PWM/MOSI, TFT2.MOSI
  N6: Part2.D13/SCK, TFT2.SCK
  GND: Part2.GND, TFT2.GND, DHT1.GND
  3V3: Part2.3V3, TFT2.VCC
  5V: Part2.5V, DHT1.VDD

custom parts:
  1.8" TFT Display with uSD: 1.8" TFT Display with SPI control and MicroSD card
